# Fritzing sketch qm-rpi-library Wiring (saved by Fritzing 0.9.9b)

parts:
  Part1 = RFID-RC522-v2
  Mod1 = Raspberry Pi 4B

nets:
  N1: Part1.SDA, Mod1.GPIO8
  N2: Part1.SCK, Mod1.GPIO11
  N3: Part1.MOSI, Mod1.GPIO10
  N4: Part1.MISO, Mod1.GPIO9
  GND: Part1.GND, Mod1.GND
  N5: Part1.RST, Mod1.GPIO25
  3.3V: Part1.3.3V, Mod1.3V3

notes:
  To Raspberry Pi 7" Touchscreen controller

custom parts:
  RFID-RC522-v2: A simple China made RFID-RC522 Reader; do check the pin labels, as this is a MFRC522 based clone.
